# Fritzing sketch pinout (saved by Fritzing 1.0.5)

parts:
  A1 = ina226 module
  U1 = LM2596 step down module
  VCC1 = Battery
  S1 = 0.91 inch OLED I2C Display 128 x 32 Pixels  # not connected
  A2 = ESP32-S3 supermini
  A3 = AHT10 module

nets:
  N1: A1.Pin_1, A1.Pin_3, A1.Pin_13, U1.IN+
  N2: A1.Pin_2, A1.Pin_12, VCC1.+
  N3: A1.Pin_5, A3.Pin_2
  N4: A1.Pin_6, A3.Pin_1
  N5: A1.Pin_7, A3.Pin_4
  N6: A1.Pin_8, A1.Pin_10, A3.Pin_3
  N7: U1.IN-, U1.OUT-, VCC1.-, A2.Pin_39
  N8: U1.OUT+, A2.Pin_40

custom parts:
  ina226 module: INA226 Voltage Current/Power Monitoring Sensor Module IIC I2C Interface Bi-directional INA226 Module CJMCU-226.
  LM2596 step down module: LM2596 DC-DC step down power supply module 3 A.
  Battery: Your standard 2x 18650 battery pack (7,4 Volts)
  ESP32-S3 supermini: Esp32-S3 Development board ESP32 SuperMini development board ESP32 Development board WiFi Bluetooth.
  AHT10 module: AHT10 Temperature Humidity Sensor Measurement Module High-Precision Digital Temp Humidity Sensor Measurement Module 1.8-6.0V I2C.
